# Fritzing sketch Practica_NFC (saved by Fritzing 1.0.4)

parts:
  A1 = ESP32-S3-WROOM-1-N16R8 dev board
  Componente1 = PN532 Elechouse RFID NFC Module V3

nets:
  N1: A1.Pin_1, A1.Pin_2, Componente1.VCC
  N2: A1.Pin_5, Componente1.SS
  N3: A1.Pin_17, Componente1.MOSI
  N4: A1.Pin_18, Componente1.SCK
  N5: A1.Pin_19, Componente1.MISO
  N6: A1.Pin_22, A1.Pin_44, Componente1.GND

custom parts:
  ESP32-S3-WROOM-1-N16R8 dev board: ESP32-S3 WIFI+BLE5.0 Development Board ESP32-S3-WROOM-1-N16R8(16M Flash/8SRAM).
  PN532 Elechouse RFID NFC Module V3: NFC is a popular technology in recent years. We often heard this work while smart phone company such as Samsung or HTC introduces their latest high-end phones. Almost all the high-end phone in the market support NFC. Near field communication (NFC) is a set of standards for smart phones and similar devices to establish radio communication with each other by touching them together or bringing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
